// Logisim project bmov4.circ as structural Verilog: 7 circuits, main circuit main
module main (
);

  wire ascii_buff_1_ttlclk, clock_1_out, core_1_ramout, core_1_writeram, d_ff_1_qn, memory_1_dataout,
       memory_1_o1, memory_1_o2, memory_1_o3, Reset_out;
  wire [6:0] ascii_buff_1_ascii;
  wire [7:0] core_1_ip, core_1_ramaddr, rom_1_data;

  D_Flip_Flop #(.trigger("high")) d_ff_1 (
    .clk(memory_1_o1), .D(clock_1_out), .Qn(d_ff_1_qn));  // open: Q, preset, reset
  Clock clock_1 (.out(clock_1_out));
  Button Reset (.out(Reset_out));
  ROM rom_1 (.addr(core_1_ip), .data(rom_1_data));
  core core_1 (
    .RamIn(memory_1_dataout), .Clock(d_ff_1_qn), .Reset(Reset_out), .Instruction(rom_1_data), .IP(core_1_ip),
    .RamAddr(core_1_ramaddr), .RamOut(core_1_ramout), .WriteRam(core_1_writeram));
  memory memory_1 (
    .Address(core_1_ramaddr), .Write(core_1_writeram), .DataIn(core_1_ramout), .Reset(Reset_out),
    .DataOut(memory_1_dataout), .O1(memory_1_o1), .O2(memory_1_o2), .O3(memory_1_o3));
  ascii_buff ascii_buff_1 (
    .Bit(memory_1_o2), .Clk(memory_1_o3), .Reset(Reset_out), .Ascii(ascii_buff_1_ascii),
    .TTLClk(ascii_buff_1_ttlclk));
  TTY #(.trigger("falling")) tty_1 (.data(ascii_buff_1_ascii), .clk(ascii_buff_1_ttlclk), .clr(Reset_out));  // open: we

  // Notes on the sheet:
  //   contents of rom_1 (hex, n*v repeats v):
  //   77 55 0 55 0 55 57 55 0 55 0 55 0 55 0 55 57 5 16 3 ba 15 b3 18 3b 19 37 15 32 57 c 17 32 45 54 57
  //   55 55 57 55 57 55 55 55 65 45 54 57 55 55 55 57 55 c5 45 54 57 55 57 55 57 55 57 55 57 25 45 54 57
  //   57 85 57 95 42 a4 57 16 37 13 c
endmodule

module dereg (
  input  [7:0] D,
  input  C,
  input  Reset,
  output [7:0] Q
);

  wire [7:0] register_1_q, register_2_q;

  Register #(.trigger("high")) register_1 (.D(D), .clk(C), .Q(register_1_q), .clr(Reset));  // open: en
  Register #(.trigger("low")) register_2 (.D(D), .clk(C), .Q(register_2_q), .clr(Reset));  // open: en
  Multiplexer #(.width(8)) multiplexer_1 (.in0(register_1_q), .in1(register_2_q), .out(Q), .sel(C));

  // Notes on the sheet:
  //   Double Edge Register
endmodule

module core (
  input  RamIn,
  input  Clock,
  input  Reset,
  input  [7:0] Instruction,
  output [7:0] IP,
  output [7:0] RamAddr,
  output RamOut,
  output WriteRam
);

  wire comparator_1_eq, comparator_3_eq, Dst3, nand_1_out, Reg0E, Reg1E, Reg2E, Reg4E, Reg5E, Reg6E, Reg7E,
       Reg8E, Reg9E, Reg10E, Reg11E, Reg12E, Reg13E, Reg14E, Reg15E;
  wire [3:0] buffer_1_out, buffer_2_out, buffer_3_out, buffer_4_out, buffer_5_out, buffer_6_out,
       buffer_7_out, buffer_8_out;
  wire [7:0] adder_1_out, Dst, multiplexer_3_out, multiplexer_4_out, multiplexer_5_out, multiplexer_6_out,
       negator_1_out, PostDst, Reg0, Reg2, Reg4, Reg5, Reg6, Reg7, Reg8, Reg9, Reg10, Reg11, Reg12, Reg13,
       Reg14, Reg15;

  assign buffer_1_out = Instruction[7:4];  // Buffer buffer_1, 4 bits wide
  assign buffer_2_out = buffer_1_out;  // Buffer buffer_2, 4 bits wide
  assign buffer_3_out = buffer_2_out;  // Buffer buffer_3, 4 bits wide
  assign buffer_4_out = buffer_3_out;  // Buffer buffer_4, 4 bits wide
  nand nand_1 (nand_1_out, RamIn, Dst3);
  Demultiplexer #(.select(4)) demultiplexer_1 (
    .out0(Reg0E), .out1(Reg1E), .out2(Reg2E), .out3(WriteRam), .out4(Reg4E), .out5(Reg5E), .out6(Reg6E),
    .out7(Reg7E), .out8(Reg8E), .out9(Reg9E), .out10(Reg10E), .out11(Reg11E), .out12(Reg12E), .out13(Reg13E),
    .out14(Reg14E), .out15(Reg15E), .in(nand_1_out), .sel(buffer_4_out));
  assign buffer_5_out = Instruction[3:0];  // Buffer buffer_5, 4 bits wide
  assign buffer_6_out = buffer_5_out;  // Buffer buffer_6, 4 bits wide
  assign buffer_7_out = buffer_6_out;  // Buffer buffer_7, 4 bits wide
  assign buffer_8_out = buffer_7_out;  // Buffer buffer_8, 4 bits wide
  Multiplexer #(.select(4), .width(8)) multiplexer_1 (
    .in0(Reg0), .in1(RamAddr), .in2(Reg2), .in3(Reg2), .in4(Reg4), .in5(Reg5), .in6(Reg6), .in7(Reg7),
    .in8(Reg8), .in9(Reg9), .in10(Reg10), .in11(Reg11), .in12(Reg12), .in13(Reg13), .in14(Reg14),
    .in15(Reg15), .out(Dst), .sel(buffer_8_out));
  Comparator #(.mode("unsigned"), .width(4)) comparator_1 (
    .a(Instruction[7:4]), .b(Instruction[3:0]), .eq(comparator_1_eq));  // open: gt, lt
  Comparator #(.mode("unsigned"), .width(4)) comparator_2 (
    .a(4'b0011), .b(Instruction[3:0]), .eq(Dst3));  // open: gt, lt
  Multiplexer #(.width(8)) multiplexer_2 (.in0(Dst), .in1(8'h1), .out(PostDst), .sel(comparator_1_eq));
  Multiplexer #(.width(8)) multiplexer_3 (.in0(Reg0), .in1(Dst), .out(multiplexer_3_out), .sel(Reg0E));
  Multiplexer #(.width(8)) multiplexer_4 (.in0(RamAddr), .in1(Dst), .out(multiplexer_4_out), .sel(Reg1E));
  not not_1 (RamOut, comparator_3_eq);
  Comparator #(.mode("unsigned")) comparator_3 (.a(Dst), .b(Reg2), .eq(comparator_3_eq));  // open: gt, lt
  Multiplexer #(.width(8)) multiplexer_5 (.in0(Reg4), .in1(negator_1_out), .out(multiplexer_5_out), .sel(Reg4E));
  Negator negator_1 (.in(Dst), .out(negator_1_out));
  Adder adder_1 (.a(Reg5), .b(Dst), .out(adder_1_out));  // open: cin, cout
  Register #(.trigger("high")) register_1 (.D(PostDst), .clk(Reg2E), .Q(Reg2), .clr(Reset));  // open: en
  Register #(.trigger("high")) register_2 (.D(PostDst), .clk(Reg10E), .Q(Reg10), .clr(Reset));  // open: en
  Multiplexer #(.width(8)) multiplexer_6 (.in0(Reg5), .in1(adder_1_out), .out(multiplexer_6_out), .sel(Reg5E));
  Register #(.trigger("high")) register_3 (.D(PostDst), .clk(Reg6E), .Q(Reg6), .clr(Reset));  // open: en
  Register #(.trigger("high")) register_4 (.D(PostDst), .clk(Reg11E), .Q(Reg11), .clr(Reset));  // open: en
  dereg dereg_1 (.D(multiplexer_3_out), .C(Clock), .Reset(Reset), .Q(IP));
  dereg dereg_2 (.D(multiplexer_4_out), .C(Clock), .Reset(Reset), .Q(RamAddr));
  Register #(.trigger("high")) register_5 (.D(PostDst), .clk(Reg7E), .Q(Reg7), .clr(Reset));  // open: en
  Register #(.trigger("high")) register_6 (.D(PostDst), .clk(Reg12E), .Q(Reg12), .clr(Reset));  // open: en
  Adder adder_2 (.a(8'h1), .b(IP), .out(Reg0));  // open: cin, cout
  dereg dereg_3 (.D(multiplexer_5_out), .C(Clock), .Reset(Reset), .Q(Reg4));
  dereg dereg_4 (.D(multiplexer_6_out), .C(Clock), .Reset(Reset), .Q(Reg5));
  Register #(.trigger("high")) register_7 (.D(PostDst), .clk(Reg8E), .Q(Reg8), .clr(Reset));  // open: en
  Register #(.trigger("high")) register_8 (.D(PostDst), .clk(Reg13E), .Q(Reg13), .clr(Reset));  // open: en
  Register #(.trigger("high")) register_9 (.D(PostDst), .clk(Reg9E), .Q(Reg9), .clr(Reset));  // open: en
  Register #(.trigger("high")) register_10 (.D(PostDst), .clk(Reg14E), .Q(Reg14), .clr(Reset));  // open: en
  Register #(.trigger("high")) register_11 (.D(PostDst), .clk(Reg15E), .Q(Reg15), .clr(Reset));  // open: en

  // Other names for the same wires on the sheet: DataIn = RamIn; Reg1[7:0] = RamAddr; Reg3[7:0] = Reg2;
  //   Reg3E = WriteRam; Rst = Reset
endmodule

module memory (
  input  [7:0] Address,
  input  Write,
  input  DataIn,
  input  Reset,
  output DataOut,
  output O1,
  output O2,
  output O3
);

  wire and_1_out, demultiplexer_1_out1, demultiplexer_1_out2, demultiplexer_1_out3, multiplexer_2_out,
       not_1_out, not_2_out, or_1_out, ram_1_dout;

  or or_1 (or_1_out, Address[7], Address[6], Address[5], Address[4], Address[3], Address[2]);
  not not_1 (not_1_out, or_1_out);
  RAM #(.dataWidth(1), .trigger("high")) ram_1 (
    .addr(Address), .we(Write), .oe(not_2_out), .din(DataIn), .dout(ram_1_dout));  // open: clk
  not not_2 (not_2_out, Write);
  and and_1 (and_1_out, not_1_out, Write);
  Demultiplexer #(.select(2)) demultiplexer_1 (
    .out1(demultiplexer_1_out1), .out2(demultiplexer_1_out2), .out3(demultiplexer_1_out3), .in(and_1_out),
    .sel(Address[1:0]));  // open: out0
  D_Flip_Flop #(.trigger("high")) d_ff_1 (
    .D(DataIn), .clk(demultiplexer_1_out1), .Q(O1), .preset(Reset));  // open: Qn, reset
  Multiplexer multiplexer_1 (.in0(ram_1_dout), .in1(multiplexer_2_out), .out(DataOut), .sel(not_1_out));
  Multiplexer #(.select(2)) multiplexer_2 (
    .in0(1'b0), .in1(O1), .in2(O2), .in3(O3), .out(multiplexer_2_out), .sel(Address[1:0]));
  D_Flip_Flop #(.trigger("high")) d_ff_2 (
    .D(DataIn), .clk(demultiplexer_1_out2), .Q(O2), .reset(Reset));  // open: Qn, preset
  and and_2 (O3, DataIn, demultiplexer_1_out3);
endmodule

module ascii_buff (
  input  Bit,
  input  Clk,
  input  Reset,
  output [6:0] Ascii,
  output TTLClk
);

  wire and_1_out, or_1_out;
  wire [7:0] aireg_1_q;

  and and_1 (and_1_out, ~Clk, TTLClk);  // AND_Gate
  Shift_Register #(.length(7), .trigger("falling")) StdoutBuff (
    .in(Bit), .clk(Clk), .out(Ascii[6]), .q0(Ascii[0]), .q1(Ascii[1]), .q2(Ascii[2]), .q3(Ascii[3]),
    .q4(Ascii[4]), .q5(Ascii[5]));  // open: shift, load, clr, d0, d1, d2, d3, d4, d5, d6, q6
  or or_1 (or_1_out, Reset, and_1_out);
  aireg aireg_1 (.C(Clk), .Reset(or_1_out), .Q(aireg_1_q));  // open: SetD, D
  Comparator comparator_1 (.a(aireg_1_q), .b(8'h7), .eq(TTLClk));  // open: gt, lt
endmodule

module aireg (
  input  SetD,
  input  [7:0] D,
  input  C,
  input  Reset,
  output [7:0] Q
);

  wire [7:0] adder_1_out, multiplexer_1_out;

  Adder adder_1 (.a(Q), .b(8'h1), .out(adder_1_out));  // open: cin, cout
  Register register_1 (.D(multiplexer_1_out), .clk(C), .Q(Q), .clr(Reset));  // open: en
  Multiplexer #(.width(8)) multiplexer_1 (.in0(adder_1_out), .in1(D), .out(multiplexer_1_out), .sel(SetD));

  // Notes on the sheet:
  //   Autoincrementing Register
endmodule

module dereg1 (
  input  D,
  input  C,
  input  Reset,
  output Q
);

  wire d_ff_1_q, d_ff_2_q;

  D_Flip_Flop #(.trigger("high")) d_ff_1 (.D(D), .clk(C), .Q(d_ff_1_q), .reset(Reset));  // open: Qn, preset
  D_Flip_Flop #(.trigger("low")) d_ff_2 (.D(D), .clk(C), .Q(d_ff_2_q), .reset(Reset));  // open: Qn, preset
  Multiplexer multiplexer_1 (.in0(d_ff_1_q), .in1(d_ff_2_q), .out(Q), .sel(C));

  // Notes on the sheet:
  //   Double Edge Latch
endmodule
