// Logisim project bmov3.circ as structural Verilog: 7 circuits, main circuit main
module main (
);

  wire and_1_out, ascii_buff_1_ttlclk, clock_1_out, core_1_dataout, core_1_write, d_ff_1_q, memory_1_dataout,
       memory_1_o1, memory_1_o2, memory_1_o3, Reset_out;
  wire [6:0] ascii_buff_1_ascii;
  wire [7:0] core_1_address, core_1_instructionpointer, rom_1_data;

  Clock clock_1 (.out(clock_1_out));
  Button Reset (.out(Reset_out));
  D_Flip_Flop #(.trigger("high")) d_ff_1 (.clk(memory_1_o1), .D(clock_1_out), .Q(d_ff_1_q));  // open: Qn, preset, reset
  ROM rom_1 (.addr(core_1_instructionpointer), .data(rom_1_data));
  core core_1 (
    .Reset(Reset_out), .DataIn(memory_1_dataout), .Clock(d_ff_1_q), .Instruction(rom_1_data),
    .Address(core_1_address), .InstructionPointer(core_1_instructionpointer), .DataOut(core_1_dataout),
    .Write(core_1_write));
  memory memory_1 (
    .Address(core_1_address), .Write(core_1_write), .DataIn(core_1_dataout), .Reset(Reset_out),
    .DataOut(memory_1_dataout), .O1(memory_1_o1), .O2(memory_1_o2), .O3(memory_1_o3));
  ascii_buff ascii_buff_1 (
    .Bit(memory_1_o2), .Clk(memory_1_o3), .Reset(Reset_out), .Ascii(ascii_buff_1_ascii),
    .TTLClk(ascii_buff_1_ttlclk));
  TTY #(.trigger("falling")) tty_1 (.data(ascii_buff_1_ascii), .clk(and_1_out), .clr(Reset_out));  // open: we
  and and_1 (and_1_out, ascii_buff_1_ttlclk, memory_1_o1);

  // Notes on the sheet:
  //   contents of rom_1 (hex, n*v repeats v):
  //   87 79 80 79 87 79 80 79 87 79 81 79 87 79 81 79 87 79 80 79 87 79 80 79 87 79 80 79 87 79 80 79 37
  //   2a 36 2e f6 2c 6f 2d 65 2e 65 7e e9 3b 21 64 70 80 81 79 87 79 87 79 81 79 87 79 81 79 87 79 81 79
  //   87 79 57 70 80 81 79 87 79 87 79 87 79 87 79 81 79 87 79 81 79 47 81 70 80 81 79 87 79 87 79 81 79
  //   87 79 81 79 87 79 87 79 87 79 a7 70 80 81 79 87 79 87 79 87 79 87 79 87 79 81 79 b7 71 c9 7c d9 7d
  //   e9 3b
endmodule

module dereg (
  input  [7:0] D,
  input  C,
  input  Reset,
  output [7:0] Q
);

  wire [7:0] register_1_q, register_2_q;

  Register #(.trigger("high")) register_1 (.D(D), .clk(C), .Q(register_1_q), .clr(Reset));  // open: en
  Register #(.trigger("low")) register_2 (.D(D), .clk(C), .Q(register_2_q), .clr(Reset));  // open: en
  Multiplexer #(.width(8)) multiplexer_1 (.in0(register_1_q), .in1(register_2_q), .out(Q), .sel(C));

  // Notes on the sheet:
  //   Double Edge Register
endmodule

module core (
  input  Reset,
  input  DataIn,
  input  Clock,
  input  [7:0] Instruction,
  output [7:0] Address,
  output [7:0] InstructionPointer,
  output DataOut,
  output Write
);

  wire buffer_1_out, buffer_2_out, buffer_3_out, buffer_4_out, buffer_5_out, buffer_6_out, buffer_7_out,
       buffer_8_out, buffer_9_out, buffer_10_out, buffer_11_out, buffer_12_out, buffer_13_out, buffer_14_out,
       buffer_15_out, buffer_16_out, Reg2E, Reg3E, Reg4E, Reg5E, Reg7E, Reg8E, Reg10E, Reg11E, Reg12E,
       Reg13E, Reg14E, Reg15E;
  wire [7:0] adder_1_out, multiplexer_2_out, Reg4, Reg5, Reg6, Reg7, Reg8, Reg9, Reg10, Reg11, Reg12, Reg13,
       Reg14, Reg15, SelData;

  Demultiplexer #(.select(4)) demultiplexer_1 (
    .out2(Reg2E), .out3(Reg3E), .out4(Reg4E), .out5(Reg5E), .out6(Write), .out7(Reg7E), .out8(Reg8E),
    .out10(Reg10E), .out11(Reg11E), .out12(Reg12E), .out13(Reg13E), .out14(Reg14E), .out15(Reg15E),
    .in(1'b1), .sel(Instruction[7:4]));  // open: out0, out1, out9
  Multiplexer #(.select(4), .width(8)) multiplexer_1 (
    .in0({8{1'b0}}), .in1(8'h1), .in2(Address), .in3(InstructionPointer), .in4(Reg4), .in5(Reg5), .in6(Reg6),
    .in7(Reg7), .in8(Reg8), .in9(Reg9), .in10(Reg10), .in11(Reg11), .in12(Reg12), .in13(Reg13), .in14(Reg14),
    .in15(Reg15), .out(SelData), .sel(Instruction[3:0]));
  Register #(.trigger("high")) register_1 (.D(SelData), .clk(Reg2E), .Q(Address), .clr(Reset));  // open: en
  Register #(.trigger("high")) register_2 (.D(SelData), .clk(Reg4E), .Q(Reg4), .clr(Reset));  // open: en
  Register #(.trigger("high")) register_3 (.D(SelData), .clk(Reg5E), .Q(Reg5), .clr(Reset));  // open: en
  Register #(.trigger("high")) register_4 (.D(SelData), .clk(Reg7E), .Q(Reg7), .clr(Reset));  // open: en
  Register #(.trigger("high")) register_5 (.D(SelData), .clk(Reg8E), .Q(Reg8), .clr(Reset));  // open: en
  Register #(.trigger("high")) register_6 (.D(SelData), .clk(Reg10E), .Q(Reg10), .clr(Reset));  // open: en
  Multiplexer #(.width(8)) multiplexer_2 (.in0(Reg4), .in1(Reg5), .out(multiplexer_2_out), .sel(DataIn));
  buf buffer_1 (buffer_1_out, buffer_4_out);
  Adder adder_1 (.a(Reg7), .b(Reg8), .out(adder_1_out));  // open: cin, cout
  Register #(.trigger("high")) register_7 (.D(SelData), .clk(Reg12E), .Q(Reg12), .clr(Reset));  // open: en
  Register #(.trigger("high")) register_8 (.D(SelData), .clk(Reg11E), .Q(Reg11), .clr(Reset));  // open: en
  aidereg aidereg_1 (.SetD(Reg3E), .D(SelData), .C(Clock), .Reset(Reset), .Q(InstructionPointer));
  buf buffer_2 (buffer_2_out, buffer_3_out);
  buf buffer_3 (buffer_3_out, buffer_6_out);
  buf buffer_4 (buffer_4_out, buffer_5_out);
  buf buffer_5 (buffer_5_out, buffer_2_out);
  Comparator #(.mode("unsigned")) comparator_1 (.a(SelData), .b(Reg5), .eq(DataOut));  // open: gt, lt
  buf buffer_6 (buffer_6_out, buffer_7_out);
  buf buffer_7 (buffer_7_out, buffer_8_out);
  buf buffer_8 (buffer_8_out, buffer_9_out);
  buf buffer_9 (buffer_9_out, buffer_10_out);
  Register #(.trigger("high")) register_9 (.D(SelData), .clk(Reg13E), .Q(Reg13), .clr(Reset));  // open: en
  Register #(.trigger("high")) register_10 (.D(SelData), .clk(Reg14E), .Q(Reg14), .clr(Reset));  // open: en
  dereg dereg_1 (.D(multiplexer_2_out), .C(buffer_1_out), .Reset(1'b0), .Q(Reg6));
  dereg dereg_2 (.D(adder_1_out), .C(buffer_1_out), .Reset(1'b0), .Q(Reg9));
  buf buffer_10 (buffer_10_out, buffer_11_out);
  buf buffer_11 (buffer_11_out, buffer_12_out);
  buf buffer_12 (buffer_12_out, buffer_13_out);
  buf buffer_13 (buffer_13_out, buffer_14_out);
  buf buffer_14 (buffer_14_out, buffer_15_out);
  buf buffer_15 (buffer_15_out, buffer_16_out);
  buf buffer_16 (buffer_16_out, Clock);
  Register #(.trigger("high")) register_11 (.D(SelData), .clk(Reg15E), .Q(Reg15), .clr(Reset));  // open: en

  // Other names for the same wires on the sheet: Reg2[7:0] = Address; Reg3[7:0] = InstructionPointer
endmodule

module aidereg (
  input  SetD,
  input  [7:0] D,
  input  C,
  input  Reset,
  output [7:0] Q
);

  wire [7:0] adder_1_out, multiplexer_1_out;

  Adder adder_1 (.a(Q), .b(8'h1), .out(adder_1_out));  // open: cin, cout
  Multiplexer #(.width(8)) multiplexer_1 (.in0(adder_1_out), .in1(D), .out(multiplexer_1_out), .sel(SetD));
  dereg dereg_1 (.D(multiplexer_1_out), .C(C), .Reset(Reset), .Q(Q));

  // Notes on the sheet:
  //   Autoincrementing Double Edge Register
endmodule

module memory (
  input  [7:0] Address,
  input  Write,
  input  DataIn,
  input  Reset,
  output DataOut,
  output O1,
  output O2,
  output O3
);

  wire and_1_out, demultiplexer_1_out1, demultiplexer_1_out2, demultiplexer_1_out3, multiplexer_2_out,
       not_1_out, not_2_out, or_1_out, ram_1_dout;

  or or_1 (or_1_out, Address[7], Address[6], Address[5], Address[4], Address[3], Address[2]);
  not not_1 (not_1_out, or_1_out);
  RAM #(.dataWidth(1), .trigger("high")) ram_1 (
    .addr(Address), .we(Write), .oe(not_2_out), .din(DataIn), .dout(ram_1_dout));  // open: clk
  not not_2 (not_2_out, Write);
  and and_1 (and_1_out, not_1_out, Write);
  Demultiplexer #(.select(2)) demultiplexer_1 (
    .out1(demultiplexer_1_out1), .out2(demultiplexer_1_out2), .out3(demultiplexer_1_out3), .in(and_1_out),
    .sel(Address[1:0]));  // open: out0
  D_Flip_Flop #(.trigger("high")) d_ff_1 (
    .D(DataIn), .clk(demultiplexer_1_out1), .Q(O1), .preset(Reset));  // open: Qn, reset
  Multiplexer multiplexer_1 (.in0(ram_1_dout), .in1(multiplexer_2_out), .out(DataOut), .sel(not_1_out));
  Multiplexer #(.select(2)) multiplexer_2 (
    .in0(1'b0), .in1(O1), .in2(O2), .in3(O3), .out(multiplexer_2_out), .sel(Address[1:0]));
  D_Flip_Flop #(.trigger("high")) d_ff_2 (
    .D(DataIn), .clk(demultiplexer_1_out2), .Q(O2), .reset(Reset));  // open: Qn, preset
  and and_2 (O3, DataIn, demultiplexer_1_out3);
endmodule

module ascii_buff (
  input  Bit,
  input  Clk,
  input  Reset,
  output [6:0] Ascii,
  output TTLClk
);

  wire and_1_out, or_1_out;
  wire [7:0] aireg_1_q;

  and and_1 (and_1_out, ~Clk, TTLClk);  // AND_Gate
  Shift_Register #(.length(7), .trigger("falling")) StdoutBuff (
    .in(Bit), .clk(Clk), .out(Ascii[6]), .q0(Ascii[0]), .q1(Ascii[1]), .q2(Ascii[2]), .q3(Ascii[3]),
    .q4(Ascii[4]), .q5(Ascii[5]));  // open: shift, load, clr, d0, d1, d2, d3, d4, d5, d6, q6
  or or_1 (or_1_out, Reset, and_1_out);
  aireg aireg_1 (.C(Clk), .Reset(or_1_out), .Q(aireg_1_q));  // open: SetD, D
  Comparator comparator_1 (.a(aireg_1_q), .b(8'h7), .eq(TTLClk));  // open: gt, lt
endmodule

module aireg (
  input  SetD,
  input  [7:0] D,
  input  C,
  input  Reset,
  output [7:0] Q
);

  wire [7:0] adder_1_out, multiplexer_1_out;

  Adder adder_1 (.a(Q), .b(8'h1), .out(adder_1_out));  // open: cin, cout
  Register register_1 (.D(multiplexer_1_out), .clk(C), .Q(Q), .clr(Reset));  // open: en
  Multiplexer #(.width(8)) multiplexer_1 (.in0(adder_1_out), .in1(D), .out(multiplexer_1_out), .sel(SetD));

  // Notes on the sheet:
  //   Autoincrementing Register
endmodule
