// Logisim project bit_mov_2.circ as structural Verilog: 4 circuits, main circuit memory
module main (
);

  wire ascii_buff_1_ttlclk, ClearTerminal_out, clock_1_out, core_1_dataout, core_1_write, Data, memory_1_o2,
       memory_1_o3, O1, or_1_out;
  wire [6:0] ascii_buff_1_ascii;
  wire [11:0] core_1_address;

  Clock clock_1 (.out(clock_1_out));
  or or_1 (or_1_out, clock_1_out, ~O1);  // OR_Gate
  core core_1 (
    .DataIn(Data), .Clock(or_1_out), .Address(core_1_address), .Write(core_1_write), .DataOut(core_1_dataout));
  memory memory_1 (
    .Address(core_1_address), .Write(core_1_write), .DataIn(core_1_dataout), .DataOut(Data), .O1(O1),
    .O2(memory_1_o2), .O3(memory_1_o3));
  ascii_buff ascii_buff_1 (
    .Bit(memory_1_o2), .Clk(memory_1_o3), .Ascii(ascii_buff_1_ascii), .TTLClk(ascii_buff_1_ttlclk));
  TTY tty_1 (.data(ascii_buff_1_ascii), .clk(ascii_buff_1_ttlclk), .clr(ClearTerminal_out));  // open: we
  Button ClearTerminal (.out(ClearTerminal_out));
endmodule

module memory (
  input  [11:0] Address,
  input  Write,
  input  DataIn,
  output DataOut,
  output O1,
  output O2,
  output O3
);

  wire and_1_out, demultiplexer_1_out1, demultiplexer_1_out2, demultiplexer_1_out3, multiplexer_2_out,
       not_1_out, or_1_out, ram_1_dout;

  or or_1 (or_1_out, Address[11], Address[10], Address[9], Address[8], Address[7], Address[6], Address[5], Address[4], Address[3], Address[2]);
  not not_1 (not_1_out, or_1_out);
  RAM #(.addrWidth(12), .dataWidth(1), .trigger("high")) ram_1 (
    .addr(Address), .we(Write), .oe(1'b1), .din(DataIn), .dout(ram_1_dout));  // open: clk
  and and_1 (and_1_out, Write, not_1_out);
  Demultiplexer #(.select(2)) demultiplexer_1 (
    .out1(demultiplexer_1_out1), .out2(demultiplexer_1_out2), .out3(demultiplexer_1_out3), .in(and_1_out),
    .sel(Address[1:0]));  // open: out0
  Multiplexer multiplexer_1 (.in0(ram_1_dout), .in1(multiplexer_2_out), .out(DataOut), .sel(not_1_out));
  Multiplexer #(.select(2)) multiplexer_2 (
    .in0(1'b0), .in1(O1), .in2(O2), .in3(O3), .out(multiplexer_2_out), .sel(Address[1:0]));
  D_Flip_Flop #(.trigger("high")) d_ff_1 (.D(DataIn), .clk(demultiplexer_1_out1), .Q(O1));  // open: Qn, preset, reset
  D_Flip_Flop #(.trigger("high")) d_ff_2 (.D(DataIn), .clk(demultiplexer_1_out2), .Q(O2));  // open: Qn, preset, reset
  and and_2 (O3, DataIn, demultiplexer_1_out3);
endmodule

module core (
  input  DataIn,
  input  Clock,
  output [11:0] Address,
  output Write,
  output DataOut
);

  wire counter_1_carry, demultiplexer_1_out2, demultiplexer_1_out3, demultiplexer_1_out4,
       demultiplexer_1_out5, demultiplexer_1_out6, demultiplexer_1_out8, demultiplexer_1_out9,
       demultiplexer_1_out11, demultiplexer_1_out12, demultiplexer_1_out13, demultiplexer_1_out14,
       demultiplexer_1_out15, ldclk, mv, not_1_out, or_1_out, or_2_out, rcmd, rst;
  wire [3:0] dst_q0, register_1_q, register_8_q, src_q0;
  wire [11:0] adder_1_out, adder_2_out, adder_3_out, multiplexer_1_out, multiplexer_2_out, multiplexer_3_out,
       multiplexer_5_out, reg2, reg3, reg4, reg5, reg6, reg7, reg8, reg9, reg10, reg11, reg12, reg13, reg14,
       reg15, sel;

  Shift_Register #(.length(4), .trigger("falling")) dst (
    .in(DataIn), .clk(ldclk), .out(dst_q0[3]), .q0(dst_q0[0]), .q1(dst_q0[1]), .q2(dst_q0[2]));  // open: shift, load, clr, d0, d1, d2, d3, q3
  not not_1 (not_1_out, mv);
  Demultiplexer #(.select(4)) demultiplexer_1 (
    .out2(demultiplexer_1_out2), .out3(demultiplexer_1_out3), .out4(demultiplexer_1_out4),
    .out5(demultiplexer_1_out5), .out6(demultiplexer_1_out6), .out8(demultiplexer_1_out8),
    .out9(demultiplexer_1_out9), .out11(demultiplexer_1_out11), .out12(demultiplexer_1_out12),
    .out13(demultiplexer_1_out13), .out14(demultiplexer_1_out14), .out15(demultiplexer_1_out15), .in(mv),
    .sel(register_1_q));  // open: out0, out1, out7, out10
  Button button_1 (.out(rst));
  Register #(.trigger("high"), .width(4)) register_1 (
    .D(dst_q0), .Q(register_1_q), .clk(mv), .clr(not_1_out));  // open: en
  Multiplexer #(.width(12)) multiplexer_1 (
    .in0(adder_3_out), .in1(sel), .out(multiplexer_1_out), .sel(demultiplexer_1_out4));
  Register #(.trigger("high"), .width(12)) regSrc (
    .D(sel), .clk(demultiplexer_1_out2), .Q(reg2), .clr(rst));  // open: en
  Register #(.trigger("high"), .width(12)) regDst (
    .D(sel), .clk(demultiplexer_1_out3), .Q(reg3), .clr(rst));  // open: en
  Register #(.trigger("falling"), .width(12)) regIP (
    .D(multiplexer_2_out), .clk(or_1_out), .Q(reg4), .clr(rst));  // open: en
  Multiplexer #(.width(12)) multiplexer_2 (.in0(multiplexer_1_out), .in1(12'h4), .out(multiplexer_2_out), .sel(rst));
  or or_1 (or_1_out, rst, demultiplexer_1_out4, ldclk);
  Register #(.trigger("high"), .width(12)) regElse (
    .D(sel), .en(Clock), .clk(demultiplexer_1_out5), .Q(reg5), .clr(rst));
  Register #(.trigger("high"), .width(12)) regIF (.D(sel), .en(Clock), .clk(demultiplexer_1_out6), .Q(reg6), .clr(rst));
  Register #(.trigger("high"), .width(12)) regA (.D(sel), .en(Clock), .clk(demultiplexer_1_out8), .Q(reg8), .clr(rst));
  Register #(.trigger("high"), .width(12)) regB (.D(sel), .en(Clock), .clk(demultiplexer_1_out9), .Q(reg9), .clr(rst));
  Register #(.trigger("high"), .width(12)) register_2 (
    .D(sel), .clk(demultiplexer_1_out11), .Q(reg11), .clr(rst));  // open: en
  Register #(.trigger("high"), .width(12)) register_3 (
    .D(sel), .clk(demultiplexer_1_out12), .Q(reg12), .clr(rst));  // open: en
  Register #(.trigger("high"), .width(12)) register_4 (
    .D(sel), .clk(demultiplexer_1_out13), .Q(reg13), .clr(rst));  // open: en
  Register #(.trigger("high"), .width(12)) register_5 (
    .D(sel), .clk(demultiplexer_1_out14), .Q(reg14), .clr(rst));  // open: en
  Register #(.trigger("high"), .width(12)) register_6 (
    .D(sel), .clk(demultiplexer_1_out15), .Q(reg15), .clr(rst));  // open: en
  Multiplexer #(.width(12)) multiplexer_3 (.in0(reg2), .in1(reg3), .out(multiplexer_3_out), .sel(Clock));
  Multiplexer #(.width(12)) multiplexer_4 (.in0(multiplexer_3_out), .in1(multiplexer_5_out), .out(Address), .sel(rcmd));
  Multiplexer #(.width(12)) multiplexer_5 (.in0(reg4), .in1(adder_1_out), .out(multiplexer_5_out));  // open: sel
  Adder #(.width(12)) adder_1 (.a(reg4), .b(12'h1), .out(adder_1_out));  // open: cin, cout
  Multiplexer #(.width(12)) multiplexer_6 (.in0(reg5), .in1(reg6), .out(reg7));  // open: sel
  Adder #(.width(12)) adder_2 (.a(reg8), .b(reg9), .out(adder_2_out));  // open: cin, cout
  and and_1 (Write, Clock, counter_1_carry);
  not not_2 (rcmd, counter_1_carry);
  Counter #(.max('h4), .trigger("falling"), .width(3)) counter_1 (
    .carry(counter_1_carry), .clk(Clock), .clr(rst));  // open: load, D, count, Q, up
  Adder #(.width(12)) adder_3 (.a(adder_1_out), .b(12'h1), .out(adder_3_out));  // open: cin, cout
  Register #(.trigger("high"), .width(12)) register_7 (.D(adder_2_out), .Q(reg10), .clk(Clock));  // open: en, clr
  and and_2 (mv, counter_1_carry, ~Clock);  // AND_Gate
  and and_3 (ldclk, Clock, rcmd);
  Shift_Register #(.length(4)) src (
    .in(DataIn), .clk(ldclk), .out(src_q0[3]), .q0(src_q0[0]), .q1(src_q0[1]), .q2(src_q0[2]));  // open: shift, load, clr, d0, d1, d2, d3, q3
  Register #(.trigger("high"), .width(4)) register_8 (.D(src_q0), .Q(register_8_q), .clk(mv));  // open: en, clr
  D_Flip_Flop #(.trigger("low")) d_ff_1 (.D(DataIn), .clk(or_2_out), .Q(DataOut));  // open: Qn, preset, reset
  or or_2 (or_2_out, Clock, rcmd);
  Multiplexer #(.select(4), .width(12)) multiplexer_7 (
    .in0({12{1'b0}}), .in1(12'h1), .in2(reg2), .in3(reg3), .in4(reg4), .in5(reg5), .in6(reg6), .in7(reg7),
    .in8(reg8), .in9(reg9), .in10(reg10), .in11(reg11), .in12(reg12), .in13(reg13), .in14(reg14),
    .in15(reg15), .out(sel), .sel(register_8_q));

  // Notes on the sheet:
  //   this register is
  //   just for visualization
  //   Clock - WE on registers is crunch because of logisim bug, no need to transfer them to the actual circuit
  //   this register is
  //   just for visualization
endmodule

module ascii_buff (
  input  Bit,
  input  Clk,
  output [6:0] Ascii,
  output TTLClk
);

  wire clock_1_out, not_1_out;

  Clock clock_1 (.out(clock_1_out));
  not not_1 (not_1_out, clock_1_out);
  Shift_Register #(.length(7), .trigger("falling")) StdoutBuff (
    .shift(not_1_out), .in(Bit), .clk(Clk), .out(Ascii[6]), .q0(Ascii[0]), .q1(Ascii[1]), .q2(Ascii[2]),
    .q3(Ascii[3]), .q4(Ascii[4]), .q5(Ascii[5]));  // open: load, clr, d0, d1, d2, d3, d4, d5, d6, q6
  Counter #(.max('h6), .trigger("falling"), .width(3)) counter_1 (
    .count(not_1_out), .carry(TTLClk), .clk(Clk));  // open: load, D, Q, up, clr

  // Notes on the sheet:
  //   to reset buff, set reg to 6
  //   using clock there is not necessary, but it is used because of logisim bug
endmodule
