// Logisim project bmov4rev4.circ as structural Verilog: 8 circuits, main circuit main
module main (
);

  wire ascii_buff_1_ttlclk, clock_1_out, d_ff_1_q, memory_1_dataout, memory_1_o1, memory_1_o2, memory_1_o3,
       mincore_1_ramout, mincore_1_writeram, Reset_out;
  wire [6:0] ascii_buff_1_ascii;
  wire [7:0] mincore_1_ip, mincore_1_ramaddr, rom_1_data;

  Button Reset (.out(Reset_out));
  D_Flip_Flop #(.trigger("high")) d_ff_1 (.clk(memory_1_o1), .D(clock_1_out), .Q(d_ff_1_q));  // open: Qn, preset, reset
  Clock clock_1 (.out(clock_1_out));
  ROM rom_1 (.addr(mincore_1_ip), .data(rom_1_data));
  mincore mincore_1 (
    .Instruction(rom_1_data), .Reset(Reset_out), .Clock(d_ff_1_q), .RamIn(memory_1_dataout),
    .IP(mincore_1_ip), .RamAddr(mincore_1_ramaddr), .WriteRam(mincore_1_writeram), .RamOut(mincore_1_ramout));
  memory memory_1 (
    .Address(mincore_1_ramaddr), .Write(mincore_1_writeram), .DataIn(mincore_1_ramout), .Reset(Reset_out),
    .DataOut(memory_1_dataout), .O1(memory_1_o1), .O2(memory_1_o2), .O3(memory_1_o3));
  ascii_buff ascii_buff_1 (
    .Bit(memory_1_o2), .Clk(memory_1_o3), .Reset(Reset_out), .Ascii(ascii_buff_1_ascii),
    .TTLClk(ascii_buff_1_ttlclk));
  TTY #(.trigger("falling")) tty_1 (.data(ascii_buff_1_ascii), .clk(ascii_buff_1_ttlclk), .clr(Reset_out));  // open: we

  // Notes on the sheet:
  //   contents of rom_1 (hex, n*v repeats v):
  //   77 0 11 0 11 0 7 0 11 0 11 0 11 0 11 0 7 10 36 14 ba 30 b4 38 4b 39 47 30 45 7 1c 37 45 20 2 7 0 0 7
  //   0 7 0 0 0 60 20 2 7 0 0 0 7 0 c0 20 2 7 0 7 0 7 0 7 0 7 50 20 2 7 7 80 7 90 25 a2 7 36 47 1c
endmodule

module dereg (
  input  [7:0] D,
  input  C,
  input  Reset,
  output [7:0] Q
);

  wire [7:0] register_1_q, register_2_q;

  Register #(.trigger("high")) register_1 (.D(D), .clk(C), .Q(register_1_q), .clr(Reset));  // open: en
  Register #(.trigger("low")) register_2 (.D(D), .clk(C), .Q(register_2_q), .clr(Reset));  // open: en
  Multiplexer #(.width(8)) multiplexer_1 (.in0(register_1_q), .in1(register_2_q), .out(Q), .sel(C));

  // Notes on the sheet:
  //   Double Edge Register
endmodule

module core (
  input  [7:0] Instruction,
  input  Reset,
  input  Clock,
  input  RamIn,
  output [7:0] IP,
  output [7:0] RamAddr,
  output WriteRam,
  output RamOut
);

  wire comparator_1_eq, comparator_3_eq, DstCond, nand_1_out, Reg0E, Reg1E, Reg2E, Reg3E, Reg5E, Reg6E,
       Reg7E, Reg8E, Reg9E, Reg10E, Reg11E, Reg12E, Reg13E, Reg14E, Reg15E;
  wire [3:0] buffer_1_out, buffer_2_out, buffer_3_out, buffer_4_out, buffer_5_out, buffer_6_out,
       buffer_7_out, buffer_8_out;
  wire [7:0] adder_1_out, Dst, multiplexer_3_out, multiplexer_4_out, multiplexer_5_out, multiplexer_6_out,
       negator_1_out, PostDst, Reg0, Reg1, Reg2, Reg4, Reg6, Reg7, Reg8, Reg9, Reg10, Reg11, Reg12, Reg13,
       Reg14, Reg15;

  assign buffer_1_out = Instruction[7:4];  // Buffer buffer_1, 4 bits wide
  assign buffer_2_out = buffer_1_out;  // Buffer buffer_2, 4 bits wide
  assign buffer_3_out = buffer_2_out;  // Buffer buffer_3, 4 bits wide
  assign buffer_4_out = buffer_3_out;  // Buffer buffer_4, 4 bits wide
  nand nand_1 (nand_1_out, RamIn, DstCond);
  Demultiplexer #(.select(4)) demultiplexer_1 (
    .out0(Reg0E), .out1(Reg1E), .out2(Reg2E), .out3(Reg3E), .out4(WriteRam), .out5(Reg5E), .out6(Reg6E),
    .out7(Reg7E), .out8(Reg8E), .out9(Reg9E), .out10(Reg10E), .out11(Reg11E), .out12(Reg12E), .out13(Reg13E),
    .out14(Reg14E), .out15(Reg15E), .in(nand_1_out), .sel(buffer_4_out));
  Comparator #(.mode("unsigned"), .width(4)) comparator_1 (
    .a(Instruction[7:4]), .b(Instruction[3:0]), .eq(comparator_1_eq));  // open: gt, lt
  Comparator #(.mode("unsigned"), .width(4)) comparator_2 (
    .a(4'b0100), .b(Instruction[3:0]), .eq(DstCond));  // open: gt, lt
  assign buffer_5_out = Instruction[3:0];  // Buffer buffer_5, 4 bits wide
  assign buffer_6_out = buffer_5_out;  // Buffer buffer_6, 4 bits wide
  assign buffer_7_out = buffer_6_out;  // Buffer buffer_7, 4 bits wide
  assign buffer_8_out = buffer_7_out;  // Buffer buffer_8, 4 bits wide
  Multiplexer #(.select(4), .width(8)) multiplexer_1 (
    .in0(Reg0), .in1(Reg1), .in2(Reg2), .in3(RamAddr), .in4(Reg4), .in5(Reg4), .in6(Reg6), .in7(Reg7),
    .in8(Reg8), .in9(Reg9), .in10(Reg10), .in11(Reg11), .in12(Reg12), .in13(Reg13), .in14(Reg14),
    .in15(Reg15), .out(Dst), .sel(buffer_8_out));
  Multiplexer #(.width(8)) multiplexer_2 (.in0(Dst), .in1(8'h1), .out(PostDst), .sel(comparator_1_eq));
  Adder adder_1 (.a(Reg0), .b(Dst), .out(adder_1_out));  // open: cin, cout
  Multiplexer #(.width(8)) multiplexer_3 (.in0(Reg1), .in1(Dst), .out(multiplexer_3_out), .sel(Reg1E));
  Negator negator_1 (.in(Dst), .out(negator_1_out));
  Multiplexer #(.width(8)) multiplexer_4 (.in0(RamAddr), .in1(PostDst), .out(multiplexer_4_out), .sel(Reg3E));
  Comparator #(.mode("unsigned")) comparator_3 (.a(PostDst), .b(Reg4), .eq(comparator_3_eq));  // open: gt, lt
  Register #(.trigger("high")) register_1 (.D(PostDst), .clk(Reg5E), .Q(Reg4));  // open: en, clr
  Register #(.trigger("high")) register_2 (.D(PostDst), .clk(Reg10E), .Q(Reg10));  // open: en, clr
  Multiplexer #(.width(8)) multiplexer_5 (.in0(Reg0), .in1(adder_1_out), .out(multiplexer_5_out), .sel(Reg0E));
  Multiplexer #(.width(8)) multiplexer_6 (.in0(Reg2), .in1(negator_1_out), .out(multiplexer_6_out), .sel(Reg2E));
  not not_1 (RamOut, comparator_3_eq);
  Register #(.trigger("high")) register_3 (.D(PostDst), .clk(Reg6E), .Q(Reg6));  // open: en, clr
  Register #(.trigger("high")) register_4 (.D(PostDst), .clk(Reg11E), .Q(Reg11));  // open: en, clr
  Register #(.trigger("high")) register_5 (.D(PostDst), .clk(Reg7E), .Q(Reg7));  // open: en, clr
  Register #(.trigger("high")) register_6 (.D(PostDst), .clk(Reg12E), .Q(Reg12));  // open: en, clr
  dereg dereg_1 (.D(multiplexer_5_out), .C(Clock), .Q(Reg0));  // open: Reset
  Adder adder_2 (.a(8'h1), .b(IP), .out(Reg1));  // open: cin, cout
  dereg dereg_2 (.D(multiplexer_3_out), .C(Clock), .Reset(Reset), .Q(IP));
  dereg dereg_3 (.D(multiplexer_6_out), .C(Clock), .Q(Reg2));  // open: Reset
  dereg dereg_4 (.D(multiplexer_4_out), .C(Clock), .Q(RamAddr));  // open: Reset
  Register #(.trigger("high")) register_7 (.D(PostDst), .clk(Reg8E), .Q(Reg8));  // open: en, clr
  Register #(.trigger("high")) register_8 (.D(PostDst), .clk(Reg13E), .Q(Reg13));  // open: en, clr
  Register #(.trigger("high")) register_9 (.D(PostDst), .clk(Reg9E), .Q(Reg9));  // open: en, clr
  Register #(.trigger("high")) register_10 (.D(PostDst), .clk(Reg14E), .Q(Reg14));  // open: en, clr
  Register #(.trigger("high")) register_11 (.D(PostDst), .clk(Reg15E), .Q(Reg15));  // open: en, clr

  // Other names for the same wires on the sheet: DataIn = RamIn; Reg3[7:0] = RamAddr; Reg4E = WriteRam;
  //   Reg5[7:0] = Reg4; Rst = Reset
endmodule

module memory (
  input  [7:0] Address,
  input  Write,
  input  DataIn,
  input  Reset,
  output DataOut,
  output O1,
  output O2,
  output O3
);

  wire and_1_out, demultiplexer_1_out1, demultiplexer_1_out2, demultiplexer_1_out3, multiplexer_2_out,
       not_1_out, not_2_out, or_1_out, ram_1_dout;

  or or_1 (or_1_out, Address[7], Address[6], Address[5], Address[4], Address[3], Address[2]);
  not not_1 (not_1_out, or_1_out);
  RAM #(.dataWidth(1), .trigger("high")) ram_1 (
    .addr(Address), .we(Write), .oe(not_2_out), .din(DataIn), .dout(ram_1_dout));  // open: clk
  not not_2 (not_2_out, Write);
  and and_1 (and_1_out, not_1_out, Write);
  Demultiplexer #(.select(2)) demultiplexer_1 (
    .out1(demultiplexer_1_out1), .out2(demultiplexer_1_out2), .out3(demultiplexer_1_out3), .in(and_1_out),
    .sel(Address[1:0]));  // open: out0
  D_Flip_Flop #(.trigger("high")) d_ff_1 (
    .D(DataIn), .clk(demultiplexer_1_out1), .Q(O1), .preset(Reset));  // open: Qn, reset
  Multiplexer multiplexer_1 (.in0(ram_1_dout), .in1(multiplexer_2_out), .out(DataOut), .sel(not_1_out));
  Multiplexer #(.select(2)) multiplexer_2 (
    .in0(ram_1_dout), .in1(O1), .in2(O2), .in3(O3), .out(multiplexer_2_out), .sel(Address[1:0]));
  D_Flip_Flop #(.trigger("high")) d_ff_2 (
    .D(DataIn), .clk(demultiplexer_1_out2), .Q(O2), .reset(Reset));  // open: Qn, preset
  and and_2 (O3, DataIn, demultiplexer_1_out3);
endmodule

module ascii_buff (
  input  Bit,
  input  Clk,
  input  Reset,
  output [6:0] Ascii,
  output TTLClk
);

  wire and_1_out, or_1_out;
  wire [7:0] aireg_1_q;

  and and_1 (and_1_out, ~Clk, TTLClk);  // AND_Gate
  Shift_Register #(.length(7), .trigger("falling")) StdoutBuff (
    .in(Bit), .clk(Clk), .out(Ascii[6]), .q0(Ascii[0]), .q1(Ascii[1]), .q2(Ascii[2]), .q3(Ascii[3]),
    .q4(Ascii[4]), .q5(Ascii[5]));  // open: shift, load, clr, d0, d1, d2, d3, d4, d5, d6, q6
  or or_1 (or_1_out, Reset, and_1_out);
  aireg aireg_1 (.C(Clk), .Reset(or_1_out), .Q(aireg_1_q));  // open: SetD, D
  Comparator comparator_1 (.a(aireg_1_q), .b(8'h7), .eq(TTLClk));  // open: gt, lt
endmodule

module aireg (
  input  SetD,
  input  [7:0] D,
  input  C,
  input  Reset,
  output [7:0] Q
);

  wire [7:0] adder_1_out, multiplexer_1_out;

  Adder adder_1 (.a(Q), .b(8'h1), .out(adder_1_out));  // open: cin, cout
  Register register_1 (.D(multiplexer_1_out), .clk(C), .Q(Q), .clr(Reset));  // open: en
  Multiplexer #(.width(8)) multiplexer_1 (.in0(adder_1_out), .in1(D), .out(multiplexer_1_out), .sel(SetD));

  // Notes on the sheet:
  //   Autoincrementing Register
endmodule

module dereg1 (
  input  D,
  input  C,
  input  Reset,
  output Q
);

  wire d_ff_1_q, d_ff_2_q;

  D_Flip_Flop #(.trigger("high")) d_ff_1 (.D(D), .clk(C), .Q(d_ff_1_q), .reset(Reset));  // open: Qn, preset
  D_Flip_Flop #(.trigger("low")) d_ff_2 (.D(D), .clk(C), .Q(d_ff_2_q), .reset(Reset));  // open: Qn, preset
  Multiplexer multiplexer_1 (.in0(d_ff_1_q), .in1(d_ff_2_q), .out(Q), .sel(C));

  // Notes on the sheet:
  //   Double Edge Latch
endmodule

module mincore (
  input  [7:0] Instruction,
  input  Reset,
  input  Clock,
  input  RamIn,
  output [7:0] IP,
  output [7:0] RamAddr,
  output WriteRam,
  output RamOut
);

  wire comparator_1_eq, comparator_2_eq, comparator_3_eq, demultiplexer_1_out0, demultiplexer_1_out1,
       demultiplexer_1_out2, demultiplexer_1_out3, demultiplexer_1_out5, demultiplexer_1_out6,
       demultiplexer_1_out7, demultiplexer_1_out8, demultiplexer_1_out9, demultiplexer_1_out10,
       demultiplexer_1_out11, demultiplexer_1_out12, demultiplexer_1_out13, demultiplexer_1_out14,
       demultiplexer_1_out15, nand_1_out;
  wire [3:0] buffer_1_out, buffer_2_out, buffer_3_out, buffer_4_out, buffer_5_out, buffer_6_out,
       buffer_7_out, buffer_8_out;
  wire [7:0] adder_1_out, adder_2_out, dereg_1_q, dereg_3_q, multiplexer_1_out, multiplexer_2_out,
       multiplexer_3_out, multiplexer_4_out, multiplexer_5_out, multiplexer_6_out, negator_1_out,
       register_1_q, register_2_q, register_3_q, register_4_q, register_5_q, register_6_q, register_7_q,
       register_8_q, register_9_q, register_10_q, register_11_q;

  assign buffer_1_out = Instruction[7:4];  // Buffer buffer_1, 4 bits wide
  assign buffer_2_out = buffer_1_out;  // Buffer buffer_2, 4 bits wide
  assign buffer_3_out = buffer_2_out;  // Buffer buffer_3, 4 bits wide
  assign buffer_4_out = buffer_3_out;  // Buffer buffer_4, 4 bits wide
  nand nand_1 (nand_1_out, comparator_3_eq, RamIn);
  Demultiplexer #(.select(4)) demultiplexer_1 (
    .out0(demultiplexer_1_out0), .out1(demultiplexer_1_out1), .out2(demultiplexer_1_out2),
    .out3(demultiplexer_1_out3), .out4(WriteRam), .out5(demultiplexer_1_out5), .out6(demultiplexer_1_out6),
    .out7(demultiplexer_1_out7), .out8(demultiplexer_1_out8), .out9(demultiplexer_1_out9),
    .out10(demultiplexer_1_out10), .out11(demultiplexer_1_out11), .out12(demultiplexer_1_out12),
    .out13(demultiplexer_1_out13), .out14(demultiplexer_1_out14), .out15(demultiplexer_1_out15),
    .in(nand_1_out), .sel(buffer_4_out));
  Adder adder_1 (.a(dereg_1_q), .b(multiplexer_5_out), .out(adder_1_out));  // open: cin, cout
  Multiplexer #(.width(8)) multiplexer_1 (
    .in0(adder_2_out), .in1(multiplexer_5_out), .out(multiplexer_1_out), .sel(demultiplexer_1_out1));
  Negator negator_1 (.in(multiplexer_5_out), .out(negator_1_out));
  Multiplexer #(.width(8)) multiplexer_2 (
    .in0(RamAddr), .in1(multiplexer_6_out), .out(multiplexer_2_out), .sel(demultiplexer_1_out3));
  Register #(.trigger("high")) register_1 (
    .D(multiplexer_6_out), .clk(demultiplexer_1_out5), .Q(register_1_q));  // open: en, clr
  Register #(.trigger("high")) register_2 (
    .D(multiplexer_6_out), .clk(demultiplexer_1_out7), .Q(register_2_q));  // open: en, clr
  Register #(.trigger("high")) register_3 (
    .D(multiplexer_6_out), .clk(demultiplexer_1_out9), .Q(register_3_q));  // open: en, clr
  Register #(.trigger("high")) register_4 (
    .D(multiplexer_6_out), .clk(demultiplexer_1_out11), .Q(register_4_q));  // open: en, clr
  Register #(.trigger("high")) register_5 (
    .D(multiplexer_6_out), .clk(demultiplexer_1_out13), .Q(register_5_q));  // open: en, clr
  Register #(.trigger("high")) register_6 (
    .D(multiplexer_6_out), .clk(demultiplexer_1_out15), .Q(register_6_q));  // open: en, clr
  Multiplexer #(.width(8)) multiplexer_3 (
    .in0(dereg_1_q), .in1(adder_1_out), .out(multiplexer_3_out), .sel(demultiplexer_1_out0));
  Multiplexer #(.width(8)) multiplexer_4 (
    .in0(dereg_3_q), .in1(negator_1_out), .out(multiplexer_4_out), .sel(demultiplexer_1_out2));
  Register #(.trigger("high")) register_7 (
    .D(multiplexer_6_out), .clk(demultiplexer_1_out6), .Q(register_7_q));  // open: en, clr
  Register #(.trigger("high")) register_8 (
    .D(multiplexer_6_out), .clk(demultiplexer_1_out8), .Q(register_8_q));  // open: en, clr
  Register #(.trigger("high")) register_9 (
    .D(multiplexer_6_out), .clk(demultiplexer_1_out10), .Q(register_9_q));  // open: en, clr
  Register #(.trigger("high")) register_10 (
    .D(multiplexer_6_out), .clk(demultiplexer_1_out12), .Q(register_10_q));  // open: en, clr
  Register #(.trigger("high")) register_11 (
    .D(multiplexer_6_out), .clk(demultiplexer_1_out14), .Q(register_11_q));  // open: en, clr
  not not_1 (RamOut, comparator_1_eq);
  Comparator #(.mode("unsigned")) comparator_1 (
    .a(multiplexer_6_out), .b(register_1_q), .eq(comparator_1_eq));  // open: gt, lt
  dereg dereg_1 (.D(multiplexer_3_out), .C(Clock), .Reset(Reset), .Q(dereg_1_q));
  Adder adder_2 (.a(8'h1), .b(IP), .out(adder_2_out));  // open: cin, cout
  dereg dereg_2 (.D(multiplexer_1_out), .C(Clock), .Q(IP));  // open: Reset
  dereg dereg_3 (.D(multiplexer_4_out), .C(Clock), .Q(dereg_3_q));  // open: Reset
  dereg dereg_4 (.D(multiplexer_2_out), .C(Clock), .Q(RamAddr));  // open: Reset
  assign buffer_5_out = Instruction[3:0];  // Buffer buffer_5, 4 bits wide
  assign buffer_6_out = buffer_5_out;  // Buffer buffer_6, 4 bits wide
  assign buffer_7_out = buffer_6_out;  // Buffer buffer_7, 4 bits wide
  assign buffer_8_out = buffer_7_out;  // Buffer buffer_8, 4 bits wide
  Multiplexer #(.select(4), .width(8)) multiplexer_5 (
    .in0(dereg_1_q), .in1(adder_2_out), .in2(dereg_3_q), .in3(RamAddr), .in4(register_1_q),
    .in5(register_1_q), .in6(register_7_q), .in7(register_2_q), .in8(register_8_q), .in9(register_3_q),
    .in10(register_9_q), .in11(register_4_q), .in12(register_10_q), .in13(register_5_q),
    .in14(register_11_q), .in15(register_6_q), .out(multiplexer_5_out), .sel(buffer_8_out));
  Comparator #(.mode("unsigned"), .width(4)) comparator_2 (
    .a(Instruction[7:4]), .b(Instruction[3:0]), .eq(comparator_2_eq));  // open: gt, lt
  Comparator #(.mode("unsigned"), .width(4)) comparator_3 (
    .a(4'b0100), .b(Instruction[3:0]), .eq(comparator_3_eq));  // open: gt, lt
  Multiplexer #(.width(8)) multiplexer_6 (
    .in0(multiplexer_5_out), .in1(8'h1), .out(multiplexer_6_out), .sel(comparator_2_eq));
endmodule
